// Logisim project dot.circ as structural Verilog: 1 circuit, main circuit main
module main (
  input  X,
  input  Y,
  input  Z,
  input  in_4,
  input  in_5,
  output out_6
);

  wire and_1_out, and_2_out, or_1_out, or_2_out, xor_1_out;

  and and_1 (and_1_out, X, Y);
  or or_1 (or_1_out, and_1_out, Z);
  xor xor_1 (xor_1_out, X, or_1_out);
  and and_2 (and_2_out, in_4, xor_1_out);
  or or_2 (or_2_out, and_2_out, in_5);
  xor xor_2 (out_6, in_4, or_2_out);

  // Notes on the sheet:
  //   x ⊕ (z ∨ x ∧ y)
endmodule
