// Logisim project Backup.circ as structural Verilog: 1 circuit, main circuit main
module main (
  input  x,
  input  y,
  input  z,
  output out_4
);

  wire nand_1_out, nand_2_out, nand_3_out, nand_4_out, nand_5_out, nand_6_out, nand_7_out;

  Joystick joystick_1 ();  // open: x, y
  nand nand_1 (nand_1_out, x, y);
  nand nand_2 (nand_2_out, y, z);
  nand nand_3 (nand_3_out, x, z);
  nand nand_4 (nand_4_out, nand_1_out, nand_2_out, nand_3_out);
  nand nand_5 (nand_5_out, x, nand_4_out);
  nand nand_6 (nand_6_out, nand_4_out, z);
  nand nand_7 (nand_7_out, x, z);
  LED led_1 (.in(out_4));
  nand nand_8 (out_4, nand_5_out, nand_6_out, nand_7_out);
endmodule
